// Logisim project 1 lab.circ as structural Verilog: 21 circuits, main circuit my_and
module my_and (
  input  in_1,
  input  in_2,
  output out_3
);

  and and_1 (out_3, in_1, in_2);
endmodule

module my_or (
  input  in_1,
  input  in_2,
  output out_3
);

  or or_1 (out_3, in_1, in_2);
endmodule

module my_xor (
  input  in_1,
  input  in_2,
  output out_3
);

  wire and_1_out, not_1_out, or_1_out;

  not not_1 (not_1_out, and_1_out);
  and and_1 (and_1_out, in_1, in_2);
  or or_1 (or_1_out, in_1, in_2);
  and and_2 (out_3, not_1_out, or_1_out);
endmodule

module my_not (
  input  in_1,
  output out_2
);

  not not_1 (out_2, in_1);
endmodule

module _1bit (
  input  in_1,
  input  in_2,
  output out_3
);

  wire not_1_out;

  and and_1 (out_3, in_1, not_1_out);
  not not_1 (not_1_out, in_2);
endmodule

module _1bit_2 (
  input  in_1,
  input  in_2,
  output out_3
);

  wire not_1_out;

  not not_1 (not_1_out, in_1);
  and and_1 (out_3, not_1_out, in_2);
endmodule

module _1bit_2_2 (
  input  in_1,
  input  in_2,
  output out_3
);

  xnor xnor_1 (out_3, in_1, in_2);
endmodule

module _1bit_2_2_2 (
  input  in_1,
  input  in_2,
  output out_3
);

  wire n1bit_1_out_3, n1bit_2_out_3;

  _1bit u_1bit_1 (.in_1(in_1), .in_2(in_2), .out_3(n1bit_1_out_3));
  _1bit_2_2 u_1bit_2 (.in_1(in_1), .in_2(in_2), .out_3(n1bit_2_out_3));
  or or_1 (out_3, n1bit_1_out_3, n1bit_2_out_3);
endmodule

module _1bit_2_2_2_2 (
  input  in_1,
  input  in_2,
  output out_3
);

  wire n1bit_1_out_3, n1bit_2_out_3;

  _1bit_2 u_1bit_1 (.in_1(in_1), .in_2(in_2), .out_3(n1bit_1_out_3));
  _1bit_2_2 u_1bit_2 (.in_1(in_1), .in_2(in_2), .out_3(n1bit_2_out_3));
  or or_1 (out_3, n1bit_1_out_3, n1bit_2_out_3);
endmodule

module _8bit (
  input  [7:0] in_1,
  input  [7:0] in_2,
  output out_3
);

  wire n1bit_1_out_3, n1bit_2_out_3, n1bit_3_out_3, n1bit_4_out_3, n1bit_5_out_3, n1bit_6_out_3,
       n1bit_7_out_3, n1bit_8_out_3;

  _1bit_2_2 u_1bit_1 (.in_1(in_1[0]), .in_2(in_2[0]), .out_3(n1bit_1_out_3));
  _1bit_2_2 u_1bit_2 (.in_1(in_1[1]), .in_2(in_2[1]), .out_3(n1bit_2_out_3));
  _1bit_2_2 u_1bit_3 (.in_1(in_1[2]), .in_2(in_2[2]), .out_3(n1bit_3_out_3));
  _1bit_2_2 u_1bit_4 (.in_1(in_1[3]), .in_2(in_2[3]), .out_3(n1bit_4_out_3));
  _1bit_2_2 u_1bit_5 (.in_1(in_1[4]), .in_2(in_2[4]), .out_3(n1bit_5_out_3));
  _1bit_2_2 u_1bit_6 (.in_1(in_1[5]), .in_2(in_2[5]), .out_3(n1bit_6_out_3));
  _1bit_2_2 u_1bit_7 (.in_1(in_1[6]), .in_2(in_2[6]), .out_3(n1bit_7_out_3));
  _1bit_2_2 u_1bit_8 (.in_1(in_1[7]), .in_2(in_2[7]), .out_3(n1bit_8_out_3));
  and and_1 (out_3, n1bit_1_out_3, n1bit_2_out_3, n1bit_3_out_3, n1bit_4_out_3, n1bit_5_out_3, n1bit_6_out_3, n1bit_7_out_3, n1bit_8_out_3);
endmodule

module _8bit_2 (
  input  [7:0] in_1,
  input  [7:0] in_2
);

  wire n1bit_1_out_3, n1bit_3_out_3, n1bit_4_out_3;

  _1bit u_1bit_1 (.in_1(in_1[0]), .in_2(in_2[0]), .out_3(n1bit_1_out_3));
  _1bit u_1bit_2 (.in_1(in_1[1]), .in_2(in_2[1]));  // open: out_3
  _1bit u_1bit_3 (.in_1(in_1[6]), .in_2(in_2[6]), .out_3(n1bit_3_out_3));
  _1bit u_1bit_4 (.in_1(in_1[7]), .in_2(in_2[7]), .out_3(n1bit_4_out_3));
  _1bit u_1bit_5 (.in_1(in_1[2]), .in_2(in_2[2]));  // open: out_3
  _1bit u_1bit_6 (.in_1(in_1[3]), .in_2(in_2[3]));  // open: out_3
  my_or my_or_1 ();  // open: in_1, in_2, out_3
  _1bit u_1bit_7 (.in_1(in_2[4]), .in_2(in_1[4]));  // open: out_3
  _1bit u_1bit_8 (.in_1(in_1[5]), .in_2(in_2[5]));  // open: out_3
endmodule

module _1bit_2_2_2_2_2 (
  input  in_1,
  input  in_2,
  output out_3
);

  xor xor_1 (out_3, in_1, in_2);
endmodule

module half_sum (
  input  in_1,
  input  in_2,
  output S,
  output O
);

  xor xor_1 (S, in_1, in_2);
  and and_1 (O, in_1, in_2);
endmodule

module sum (
  input  in_1,
  input  in_2,
  input  in_3,
  output S,
  output O
);

  wire half_sum_1_o, half_sum_1_s, half_sum_2_o;

  half_sum half_sum_1 (.in_1(in_2), .in_2(in_3), .S(half_sum_1_s), .O(half_sum_1_o));
  half_sum half_sum_2 (.in_1(in_1), .in_2(half_sum_1_s), .S(S), .O(half_sum_2_o));
  or or_1 (O, half_sum_2_o, half_sum_1_o);
endmodule

module _8bit_2_2 (
  input  [7:0] in_1,
  input  [7:0] in_2,
  output [7:0] S,
  output _0
);

  wire half_sum_1_o, sum_1_o, sum_2_o, sum_3_o, sum_4_o, sum_5_o, sum_6_o;

  half_sum half_sum_1 (.in_1(in_1[0]), .in_2(in_2[0]), .S(S[0]), .O(half_sum_1_o));
  sum sum_1 (.in_1(half_sum_1_o), .in_2(in_1[1]), .in_3(in_2[1]), .S(S[1]), .O(sum_1_o));
  sum sum_2 (.in_1(sum_1_o), .in_2(in_1[2]), .in_3(in_2[2]), .S(S[2]), .O(sum_2_o));
  sum sum_3 (.in_1(sum_2_o), .in_2(in_1[3]), .in_3(in_2[3]), .S(S[3]), .O(sum_3_o));
  sum sum_4 (.in_1(sum_3_o), .in_2(in_1[4]), .in_3(in_2[4]), .S(S[4]), .O(sum_4_o));
  sum sum_5 (.in_1(sum_4_o), .in_2(in_1[5]), .in_3(in_2[5]), .S(S[5]), .O(sum_5_o));
  sum sum_6 (.in_1(sum_5_o), .in_2(in_1[6]), .in_3(in_2[6]), .S(S[6]), .O(sum_6_o));
  sum sum_7 (.in_1(sum_6_o), .in_2(in_1[7]), .in_3(in_2[7]), .S(S[7]), .O(_0));
endmodule

module half_minus (
  input  in_1,
  input  in_2,
  output R,
  output N
);

  wire not_1_out;

  not not_1 (not_1_out, in_1);
  xor xor_1 (R, in_1, in_2);
  and and_1 (N, not_1_out, in_2);
endmodule

module minus (
  input  in_1,
  input  in_2,
  input  in_3,
  output R,
  output A
);

  wire and_1_out, half_minus_1_n, not_1_out, xor_1_out;

  not not_1 (not_1_out, in_2);
  xor xor_1 (xor_1_out, in_1, in_2);
  and and_1 (and_1_out, in_1, not_1_out);
  half_minus half_minus_1 (.in_1(xor_1_out), .in_2(in_3), .R(R), .N(half_minus_1_n));
  or or_1 (A, and_1_out, half_minus_1_n);
endmodule

module _8bit_2_2_2 (
  input  [7:0] in_1,
  input  [7:0] in_2,
  output [7:0] S,
  output _0
);

  wire half_minus_1_n, minus_1_a, minus_2_a, minus_3_a, minus_4_a, minus_5_a, minus_6_a;

  half_minus half_minus_1 (.in_1(in_1[0]), .in_2(in_2[0]), .R(S[0]), .N(half_minus_1_n));
  minus minus_1 (.in_1(half_minus_1_n), .in_2(in_1[1]), .in_3(in_2[1]), .R(S[1]), .A(minus_1_a));
  minus minus_2 (.in_1(minus_1_a), .in_2(in_1[2]), .in_3(in_2[2]), .R(S[2]), .A(minus_2_a));
  minus minus_3 (.in_1(minus_2_a), .in_2(in_1[3]), .in_3(in_2[3]), .R(S[3]), .A(minus_3_a));
  minus minus_4 (.in_1(minus_3_a), .in_2(in_1[4]), .in_3(in_2[4]), .R(S[4]), .A(minus_4_a));
  minus minus_5 (.in_1(minus_4_a), .in_2(in_1[5]), .in_3(in_2[5]), .R(S[5]), .A(minus_5_a));
  minus minus_6 (.in_1(minus_5_a), .in_2(in_1[6]), .in_3(in_2[6]), .R(S[6]), .A(minus_6_a));
  minus minus_7 (.in_1(minus_6_a), .in_2(in_1[7]), .in_3(in_2[7]), .R(S[7]), .A(_0));
endmodule

module circuit (
  input  in_1,
  output out_2,
  output out_3
);

  half_sum half_sum_1 (.in_1(1'b1), .in_2(in_1), .S(out_2), .O(out_3));
endmodule

module circuit_2 (
  input  in_1,
  output out_2,
  output out_3
);

  half_minus half_minus_1 (.in_1(in_1), .in_2(1'b1), .R(out_2), .N(out_3));
endmodule

module f8bit (
  input  [7:0] in_1,
  input  [7:0] in_2,
  output [7:0] S,
  output _0
);

  wire sum_1_o, sum_2_o, sum_3_o, sum_4_o, sum_5_o, sum_6_o, undriven;

  sum sum_1 (.in_1(undriven), .in_2(in_1[1]), .in_3(in_2[1]), .S(S[1]), .O(sum_1_o));
  sum sum_2 (.in_1(sum_1_o), .in_2(in_1[2]), .in_3(in_2[2]), .S(S[2]), .O(sum_2_o));
  sum sum_3 (.in_1(sum_2_o), .in_2(in_1[3]), .in_3(in_2[3]), .S(S[3]), .O(sum_3_o));
  sum sum_4 (.in_1(sum_3_o), .in_2(in_1[4]), .in_3(in_2[4]), .S(S[4]), .O(sum_4_o));
  sum sum_5 (.in_1(sum_4_o), .in_2(in_1[5]), .in_3(in_2[5]), .S(S[5]), .O(sum_5_o));
  sum sum_6 (.in_1(sum_5_o), .in_2(in_1[6]), .in_3(in_2[6]), .S(S[6]), .O(sum_6_o));
  sum sum_7 (.in_1(sum_6_o), .in_2(in_1[7]), .in_3(in_2[7]), .S(S[7]), .O(_0));
endmodule
