// Logisim project add with timer.circ as structural Verilog: 4 circuits, main circuit RS-triger
module RS_triger (
  input  R,
  input  S,
  output q1,
  output q2
);

  nor nor_1 (q1, R, q2);
  nor nor_2 (q2, q1, S);
endmodule

module D_latch (
  input  E,
  input  D,
  output q1,
  output q2
);

  wire and_1_out, and_2_out, not_1_out;

  not not_1 (not_1_out, D);
  and and_1 (and_1_out, not_1_out, E);
  and and_2 (and_2_out, E, D);
  RS_triger rs_triger_1 (.R(and_1_out), .S(and_2_out), .q1(q1), .q2(q2));
endmodule

module D_Flip_flop (
  input  D,
  output q1,
  output q2
);

  wire and_1_out, and_2_out, clock_1_out, not_1_out;

  not not_1 (not_1_out, D);
  Clock clock_1 (.out(clock_1_out));
  and and_1 (and_1_out, not_1_out, clock_1_out);
  and and_2 (and_2_out, clock_1_out, D);
  nor nor_1 (q1, and_1_out, q2);
  nor nor_2 (q2, q1, and_2_out);
endmodule

module _1 (
  input  [7:0] in_1,
  input  in_2,
  output [7:0] out_3
);

  wire adder_1_cout, and_1_out, button_1_out, clock_1_out, not_1_out;
  wire [7:0] adder_1_out;

  not not_1 (not_1_out, adder_1_cout);
  Clock clock_1 (.out(clock_1_out));
  Button button_1 (.out(button_1_out));
  Adder adder_1 (.a(out_3), .b(in_1), .out(adder_1_out), .cout(adder_1_cout));  // open: cin
  and and_1 (and_1_out, not_1_out, in_2);
  Register register_1 (.D(adder_1_out), .en(and_1_out), .Q(out_3), .clk(clock_1_out), .clr(button_1_out));
endmodule
