// Logisim project arithm.circ as structural Verilog: 6 circuits, main circuit half-add
module half_add (
  input  a,
  input  b,
  output S,
  output P
);

  xor xor_1 (S, a, b);
  or or_1 (P, a, b);
endmodule

module add (
  input  P,
  input  a,
  input  b,
  output S,
  output P_2
);

  wire half_add_1_p, half_add_1_s, half_add_2_p;

  half_add half_add_1 (.a(a), .b(b), .S(half_add_1_s), .P(half_add_1_p));
  half_add half_add_2 (.a(P), .b(half_add_1_s), .S(S), .P(half_add_2_p));
  or or_1 (P_2, half_add_2_p, half_add_1_p);
endmodule

module _4_bit_add (
  input  [3:0] a,
  input  [3:0] b,
  output [3:0] S,
  output p
);

  wire add_1_p_2, add_2_p_2, half_add_1_p;

  half_add half_add_1 (.a(a[0]), .b(b[0]), .S(S[0]), .P(half_add_1_p));
  add add_1 (.a(a[1]), .b(b[1]), .P(half_add_1_p), .S(S[1]), .P_2(add_1_p_2));
  add add_2 (.a(a[2]), .b(b[2]), .P(add_1_p_2), .S(S[2]), .P_2(add_2_p_2));
  add add_3 (.a(a[3]), .b(b[3]), .P(add_2_p_2), .S(S[3]), .P_2(p));
endmodule

module helf_add_s_north (
  input  a,
  input  b,
  output S,
  output P
);

  xor xor_1 (S, a, b);
  or or_1 (P, a, b);
endmodule

module MUX (
  input  a,
  input  x1,
  input  x2,
  output out_4
);

  wire and_1_out, and_2_out, not_1_out;

  not not_1 (not_1_out, a);
  and and_1 (and_1_out, not_1_out, x1);
  and and_2 (and_2_out, a, x2);
  or or_1 (out_4, and_1_out, and_2_out);
endmodule

module _4c_MUX (
  input  x1,
  input  x2,
  input  x3,
  input  x4,
  input  in_5,
  input  in_6,
  output out_7
);

  wire mux_1_out_4, mux_2_out_4;

  MUX mux_1 (.a(x1), .x1(x2), .x2(in_5), .out_4(mux_1_out_4));
  MUX mux_2 (.a(x3), .x1(x4), .x2(in_5), .out_4(mux_2_out_4));
  MUX mux_3 (.a(mux_1_out_4), .x1(mux_2_out_4), .x2(in_6), .out_4(out_7));
endmodule
